// Logisim project computer_foundation.circ as structural Verilog
module my_computer (
  input  [15:0] in_1,
  input  in_2,
  input  in_3,
  input  in_4,
  input  in_5,
  input  in_6,
  input  in_7,
  input  in_8,
  input  in_9,
  input  in_10,
  input  in_11,
  input  in_12,
  input  in_13,
  input  in_14,
  input  in_15,
  input  in_16,
  input  in_17,
  input  in_18,
  input  in_19,
  output [15:0] out_20
);

  wire clock_1_out, e_A, e_ACC, e_D, e_IAR, e_INC, e_IR, e_RAM, e_ROM, f, no, nx, ny, s_A, s_ACC, s_D, s_IAR,
       s_IR, s_RAM, s_RAM_AR, s_ROM_AR, s_TMP, zx, zy;
  wire [15:0] ALU_o, IR_o, ram_1_dout, RAM_AR_o, rom_1_data, ROM_AR_o, TMP_o;

  Clock clock_1 (.out(clock_1_out));
  my_control my_control_1 (
    .clk(clock_1_out), .instr(IR_o), .e_D(e_D), .s_D(s_D), .e_A(e_A), .s_A(s_A), .e_IAR(e_IAR),
    .s_IAR(s_IAR), .e_IR(e_IR), .s_IR(s_IR), .s_TMP(s_TMP), .e_ACC(e_ACC), .s_ACC(s_ACC),
    .s_RAM_AR(s_RAM_AR), .s_ROM_AR(s_ROM_AR), .e_RAM(e_RAM), .s_RAM(s_RAM), .e_ROM(e_ROM), .e_INC(e_INC),
    .zx(zx), .nx(nx), .zy(zy), .ny(ny), .f(f), .no(no));
  assign out_20 = in_2 ? in_1 : 16'bz;  // Controlled_Buffer controlled_buffer_1
  my_reg IAR (.i(out_20), .s(in_5), .e(in_6), .o(out_20));
  my_reg D (.i(out_20), .s(in_8), .e(in_9), .o(out_20));
  my_reg A (.i(out_20), .s(in_12), .e(in_13), .o(out_20));
  my_reg IR (.i(out_20), .s(in_14), .e(1'b1), .o(IR_o));
  assign out_20 = in_15 ? IR_o : 16'bz;  // Controlled_Buffer controlled_buffer_2
  assign out_20 = in_3 ? 16'h1 : 16'bz;  // Controlled_Buffer controlled_buffer_3
  ROM #(.addrWidth(16), .dataWidth(16)) rom_1 (.addr(ROM_AR_o), .data(rom_1_data));
  RAM #(.addrWidth(16), .dataWidth(16), .enables("line"), .trigger("high")) ram_1 (
    .addr(RAM_AR_o), .we(1'b1), .clk(in_7), .din(out_20), .dout(ram_1_dout));
  assign out_20 = in_16 ? rom_1_data : 16'bz;  // Controlled_Buffer controlled_buffer_4
  assign out_20 = in_10 ? ram_1_dout : 16'bz;  // Controlled_Buffer controlled_buffer_5
  my_reg ROM_AR (.i(out_20), .s(in_11), .e(1'b1), .o(ROM_AR_o));
  my_reg TMP (.i(out_20), .s(in_17), .e(1'b1), .o(TMP_o));
  my_reg RAM_AR (.i(out_20), .s(in_4), .e(1'b1), .o(RAM_AR_o));
  my_alu ALU (.x(out_20), .y(TMP_o), .o(ALU_o));  // open: zx, nx, zy, ny, f, no, zr, ng
  my_reg ACC (.i(ALU_o), .s(in_18), .e(in_19), .o(out_20));
endmodule

module my_reg (
  input  [15:0] i,
  input  s,
  input  e,
  output [15:0] o
);

  wire [15:0] register_1_q;

  Register #(.trigger("high"), .width(16)) register_1 (.D(i), .clk(s), .Q(register_1_q));  // open: en, clr
  assign o = e ? register_1_q : 16'bz;  // Controlled_Buffer controlled_buffer_1
endmodule

module my_alu (
  input  [15:0] x,
  input  [15:0] y,
  input  zx,
  input  nx,
  input  zy,
  input  ny,
  input  f,
  input  no,
  output [15:0] o,
  output zr,
  output ng
);

  wire or_1_out;
  wire [15:0] adder_1_out, and_1_out, multiplexer_1_out, multiplexer_2_out, multiplexer_3_out,
       multiplexer_4_out, multiplexer_5_out, not_1_out, not_2_out, not_3_out;

  Multiplexer #(.width(16)) multiplexer_1 (.in0(x), .in1({16{1'b0}}), .out(multiplexer_1_out), .sel(zx));
  Multiplexer #(.width(16)) multiplexer_2 (.in0(y), .in1({16{1'b0}}), .out(multiplexer_2_out), .sel(zy));
  assign not_1_out = ~multiplexer_1_out;  // NOT_Gate not_1, 16 bits wide
  assign not_2_out = ~multiplexer_2_out;  // NOT_Gate not_2, 16 bits wide
  Multiplexer #(.width(16)) multiplexer_3 (.in0(multiplexer_1_out), .in1(not_1_out), .out(multiplexer_3_out), .sel(nx));
  Multiplexer #(.width(16)) multiplexer_4 (.in0(multiplexer_2_out), .in1(not_2_out), .out(multiplexer_4_out), .sel(ny));
  Adder #(.width(16)) adder_1 (.a(multiplexer_3_out), .b(multiplexer_4_out), .out(adder_1_out));  // open: cin, cout
  assign and_1_out = multiplexer_3_out & multiplexer_4_out;  // AND_Gate and_1, 16 bits wide
  Multiplexer #(.width(16)) multiplexer_5 (.in0(and_1_out), .in1(adder_1_out), .out(multiplexer_5_out), .sel(f));
  Multiplexer #(.width(16)) multiplexer_6 (.in0(multiplexer_5_out), .in1(not_3_out), .out({ng, o[14:0]}), .sel(no));
  assign not_3_out = ~multiplexer_5_out;  // NOT_Gate not_3, 16 bits wide
  or or_1 (or_1_out, o[0], o[1], o[2], o[3], o[4], o[5], o[6], o[7], o[8], o[9], o[10], o[11], o[12], o[13], o[14], ng);
  not not_4 (zr, or_1_out);

  assign o[15] = ng;
endmodule

module my_clock (
  input  clk,
  output next_step,
  output enable,
  output set
);

  wire d_ff_1_q, not_1_out, not_2_out;

  D_Flip_Flop d_ff_1 (.D(not_2_out), .clk(not_1_out), .Q(d_ff_1_q));  // open: Qn, preset, reset
  not not_1 (not_1_out, clk);
  not not_2 (not_2_out, enable);
  D_Flip_Flop #(.trigger("high")) d_ff_2 (.D(d_ff_1_q), .clk(clk), .Q(enable));  // open: Qn, preset, reset
  and and_1 (set, enable, clk);
  not not_3 (next_step, enable);
  // Digital_Oscilloscope digital_oscilloscope_1: pin names not known; wires that end beside it: clk, next_step, enable, set
endmodule

module my_control (
  input  clk,
  input  [15:0] instr,
  output e_D,
  output s_D,
  output e_A,
  output s_A,
  output e_IAR,
  output s_IAR,
  output e_IR,
  output s_IR,
  output s_TMP,
  output e_ACC,
  output s_ACC,
  output s_RAM_AR,
  output s_ROM_AR,
  output e_RAM,
  output s_RAM,
  output e_ROM,
  output e_INC,
  output zx,
  output nx,
  output zy,
  output ny,
  output f,
  output no
);

  wire e_IAR_0, e_ROM_1, enable, my_clock_1_next_step, s_IR_1, s_ROM_AR_0, set, step_0, step_1, step_2,
       step_3, step_4, step_5, step_6, step_7;
  wire [3:0] counter_1_q;

  my_clock my_clock_1 (.clk(clk), .next_step(my_clock_1_next_step), .enable(enable), .set(set));
  Counter #(.max('hf), .width(4)) counter_1 (
    .Q(counter_1_q), .clk(my_clock_1_next_step));  // open: load, D, count, carry, up, clr
  and and_1 (e_IAR_0, enable, step_0);
  Demultiplexer #(.select(4)) demultiplexer_1 (
    .out0(step_0), .out1(step_1), .out2(step_2), .out3(step_3), .out4(step_4), .out5(step_5), .out6(step_6),
    .out7(step_7), .in(1'b1), .sel(counter_1_q));  // open: out8, out9, out10, out11, out12, out13, out14, out15
  buf or_1 (e_IAR, e_IAR_0);  // OR_Gate
  and and_2 (s_ROM_AR_0, set, step_0);
  and and_3 (e_ROM_1, enable, step_1);
  buf or_2 (s_ROM_AR, s_ROM_AR_0);  // OR_Gate
  and and_4 (s_IR_1, set, step_1);
  buf or_3 (e_ROM, e_ROM_1);  // OR_Gate
  buf or_4 (s_IR, s_IR_1);  // OR_Gate
endmodule
