// Logisim project computer_hack.circ as structural Verilog
module my_computer (
  input  [15:0] in_1,
  input  in_2,
  output [15:0] out_3
);

  wire clock_1_out, e_A, e_ACC, e_D, e_IAR, e_INC, e_IR, e_RAM, e_ROM, f, ng, no, nx, ny, or_1_out, s_A,
       s_ACC, s_D, s_IAR, s_IR, s_RAM, s_RAM_AR, s_ROM_AR, s_TMP, zr, zx, zy;
  wire [14:0] ACC_o;
  wire [15:0] ALU_o, IR_o, ram_1_dout, RAM_AR_o, rom_1_data, ROM_AR_o, TMP_o;

  Clock clock_1 (.out(clock_1_out));
  my_control my_control_1 (
    .clk(clock_1_out), .instr(IR_o), .zr(zr), .ng(ng), .e_D(e_D), .s_D(s_D), .e_A(e_A), .s_A(s_A),
    .e_IAR(e_IAR), .s_IAR(s_IAR), .e_IR(e_IR), .s_IR(s_IR), .s_TMP(s_TMP), .e_ACC(e_ACC), .s_ACC(s_ACC),
    .s_RAM_AR(s_RAM_AR), .s_ROM_AR(s_ROM_AR), .e_RAM(e_RAM), .s_RAM(s_RAM), .e_ROM(e_ROM), .e_INC(e_INC),
    .zx(zx), .nx(nx), .zy(zy), .ny(ny), .f(f), .no(no));
  assign out_3 = in_2 ? in_1 : 16'bz;  // Controlled_Buffer controlled_buffer_1
  my_reg IAR (.i(out_3), .s(s_IAR), .e(e_IAR), .o(out_3));
  my_reg D (.i(out_3), .s(s_D), .e(e_D), .o(out_3));
  my_reg A (.i(out_3), .s(s_A), .e(e_A), .o(out_3));
  my_reg IR (.i(out_3), .s(s_IR), .e(1'b1), .o(IR_o));
  assign out_3 = e_IR ? IR_o : 16'bz;  // Controlled_Buffer controlled_buffer_2
  assign out_3 = e_INC ? 16'h1 : 16'bz;  // Controlled_Buffer controlled_buffer_3
  ROM #(.addrWidth(16), .dataWidth(16)) rom_1 (.addr(ROM_AR_o), .data(rom_1_data));
  RAM #(.addrWidth(16), .dataWidth(16), .enables("line"), .trigger("high")) ram_1 (
    .addr(RAM_AR_o), .we(1'b1), .clk(s_RAM), .din(out_3), .dout(ram_1_dout));
  assign out_3 = e_ROM ? rom_1_data : 16'bz;  // Controlled_Buffer controlled_buffer_4
  assign out_3 = e_RAM ? ram_1_dout : 16'bz;  // Controlled_Buffer controlled_buffer_5
  my_reg ROM_AR (.i(out_3), .s(s_ROM_AR), .e(1'b1), .o(ROM_AR_o));
  my_reg TMP (.i(out_3), .s(s_TMP), .e(1'b1), .o(TMP_o));
  my_reg RAM_AR (.i(out_3), .s(s_RAM_AR), .e(1'b1), .o(RAM_AR_o));
  assign out_3 = e_ACC ? {ng, ACC_o} : 16'bz;  // Controlled_Buffer controlled_buffer_6
  my_alu ALU (.x(TMP_o), .y(out_3), .zx(zx), .nx(nx), .zy(zy), .ny(ny), .f(f), .no(no), .o(ALU_o));  // open: zr, ng
  my_reg ACC (.i(ALU_o), .s(s_ACC), .e(1'b1), .o({ng, ACC_o}));
  or or_1 (or_1_out, ACC_o[0], ACC_o[1], ACC_o[2], ACC_o[3], ACC_o[4], ACC_o[5], ACC_o[6], ACC_o[7], ACC_o[8], ACC_o[9], ACC_o[10], ACC_o[11], ACC_o[12], ACC_o[13], ACC_o[14], ng);
  not not_1 (zr, or_1_out);

  // Notes on the sheet:
  //   contents of rom_1 (hex, n*v repeats v):
  //   0 2 ec10 3 e090 0 e308
endmodule

module my_reg (
  input  [15:0] i,
  input  s,
  input  e,
  output [15:0] o
);

  wire [15:0] register_1_q;

  Register #(.trigger("high"), .width(16)) register_1 (.D(i), .clk(s), .Q(register_1_q));  // open: en, clr
  assign o = e ? register_1_q : 16'bz;  // Controlled_Buffer controlled_buffer_1
endmodule

module my_alu (
  input  [15:0] x,
  input  [15:0] y,
  input  zx,
  input  nx,
  input  zy,
  input  ny,
  input  f,
  input  no,
  output [15:0] o,
  output zr,
  output ng
);

  wire or_1_out;
  wire [15:0] adder_1_out, and_1_out, multiplexer_1_out, multiplexer_2_out, multiplexer_3_out,
       multiplexer_4_out, multiplexer_5_out, not_1_out, not_2_out, not_3_out;

  Multiplexer #(.width(16)) multiplexer_1 (.in0(x), .in1({16{1'b0}}), .out(multiplexer_1_out), .sel(zx));
  Multiplexer #(.width(16)) multiplexer_2 (.in0(y), .in1({16{1'b0}}), .out(multiplexer_2_out), .sel(zy));
  assign not_1_out = ~multiplexer_1_out;  // NOT_Gate not_1, 16 bits wide
  assign not_2_out = ~multiplexer_2_out;  // NOT_Gate not_2, 16 bits wide
  Multiplexer #(.width(16)) multiplexer_3 (.in0(multiplexer_1_out), .in1(not_1_out), .out(multiplexer_3_out), .sel(nx));
  Multiplexer #(.width(16)) multiplexer_4 (.in0(multiplexer_2_out), .in1(not_2_out), .out(multiplexer_4_out), .sel(ny));
  Adder #(.width(16)) adder_1 (.a(multiplexer_3_out), .b(multiplexer_4_out), .out(adder_1_out));  // open: cin, cout
  assign and_1_out = multiplexer_3_out & multiplexer_4_out;  // AND_Gate and_1, 16 bits wide
  Multiplexer #(.width(16)) multiplexer_5 (.in0(and_1_out), .in1(adder_1_out), .out(multiplexer_5_out), .sel(f));
  Multiplexer #(.width(16)) multiplexer_6 (.in0(multiplexer_5_out), .in1(not_3_out), .out({ng, o[14:0]}), .sel(no));
  assign not_3_out = ~multiplexer_5_out;  // NOT_Gate not_3, 16 bits wide
  or or_1 (or_1_out, o[0], o[1], o[2], o[3], o[4], o[5], o[6], o[7], o[8], o[9], o[10], o[11], o[12], o[13], o[14], ng);
  not not_4 (zr, or_1_out);

  assign o[15] = ng;
endmodule

module my_clock (
  input  clk,
  output next_step,
  output enable,
  output set
);

  wire d_ff_1_q, not_1_out, not_2_out;

  D_Flip_Flop d_ff_1 (.D(not_2_out), .clk(not_1_out), .Q(d_ff_1_q));  // open: Qn, preset, reset
  not not_1 (not_1_out, clk);
  not not_2 (not_2_out, enable);
  D_Flip_Flop #(.trigger("high")) d_ff_2 (.D(d_ff_1_q), .clk(clk), .Q(enable));  // open: Qn, preset, reset
  and and_1 (set, enable, clk);
  not not_3 (next_step, enable);
  // Digital_Oscilloscope digital_oscilloscope_1: pin names not known; wires that end beside it: clk, next_step, enable, set
endmodule

module my_control (
  input  clk,
  input  [15:0] instr,
  input  zr,
  input  ng,
  output e_D,
  output s_D,
  output e_A,
  output s_A,
  output e_IAR,
  output s_IAR,
  output e_IR,
  output s_IR,
  output s_TMP,
  output e_ACC,
  output s_ACC,
  output s_RAM_AR,
  output s_ROM_AR,
  output e_RAM,
  output s_RAM,
  output e_ROM,
  output e_INC,
  output zx,
  output nx,
  output zy,
  output ny,
  output f,
  output no
);

  wire controlled_buffer_1_out, controlled_buffer_3_out, demultiplexer_1_out9, e_A_3, e_A_3_C, e_A_5_C,
       e_ACC_4_C, e_ACC_8, e_D_2_C, e_IAR_0, e_IAR_6, e_INC_7, e_IR_2, e_RAM_3_C, e_ROM_1, enable, f_7,
       jeq_out, jge_out, jgt_out, jle_out, jlt_out, jmp, jmp_out, jne_out, my_clock_1_next_step, not_3_out,
       not_4_out, not_5_out, not_6_out, not_7_out, not_8_out, not_9_out, not_ng, not_zr, or_12_out,
       or_15_out, or_17_out, s_A_2, s_A_4_C, s_ACC_3_C, s_ACC_7, s_D_4_C, s_IAR_5_C, s_IAR_8, s_IR_1,
       s_RAM_4_C, s_RAM_AR_3, s_ROM_AR_0, s_TMP_2_C, s_TMP_6, set, step_0, step_1, step_2, step_3, step_4,
       step_5, step_6, step_7, step_8;
  wire [3:0] counter_1_q;

  not not_1 (not_zr, zr);
  not not_2 (not_ng, ng);
  my_clock my_clock_1 (.clk(clk), .next_step(my_clock_1_next_step), .enable(enable), .set(set));
  Counter #(.max('hf), .width(4)) counter_1 (
    .Q(counter_1_q), .clk(my_clock_1_next_step), .clr(demultiplexer_1_out9));  // open: load, D, count, carry, up
  and and_1 (e_IAR_0, enable, step_0);
  and and_2 (e_IR_2, enable, step_2, not_3_out);
  and and_3 (e_D_2_C, enable, step_2, instr[15]);
  Demultiplexer #(.select(4)) demultiplexer_1 (
    .out0(step_0), .out1(step_1), .out2(step_2), .out3(step_3), .out4(step_4), .out5(step_5), .out6(step_6),
    .out7(step_7), .out8(step_8), .out9(demultiplexer_1_out9), .in(1'b1), .sel(counter_1_q));  // open: out10, out11, out12, out13, out14, out15
  not not_3 (not_3_out, instr[15]);
  or or_1 (e_IAR, e_IAR_0, e_IAR_6);
  or or_2 (s_IAR, s_IAR_5_C, s_IAR_8);
  and and_4 (s_ROM_AR_0, set, step_0);
  and and_5 (s_A_2, set, step_2, not_3_out);
  and and_6 (s_TMP_2_C, set, step_2, instr[15]);
  and and_7 (e_RAM_3_C, step_3, enable, instr[15], instr[12]);
  and and_8 (e_A_3_C, step_3, enable, instr[15], not_4_out);
  not not_4 (not_4_out, instr[12]);
  and and_9 (e_ROM_1, enable, step_1);
  and and_10 (e_A_3, enable, step_3, not_5_out);
  buf or_3 (s_ROM_AR, s_ROM_AR_0);  // OR_Gate
  not not_5 (not_5_out, instr[15]);
  and and_11 (s_IR_1, set, step_1);
  and and_12 (s_RAM_AR_3, set, step_3, not_5_out);
  and and_13 (s_ACC_3_C, set, step_3, instr[15]);
  buf or_4 (e_ROM, e_ROM_1);  // OR_Gate
  buf or_5 (e_IR, e_IR_2);  // OR_Gate
  buf or_6 (s_IR, s_IR_1);  // OR_Gate
  and and_14 (e_ACC_4_C, enable, step_4, instr[15]);
  or or_7 (e_A, e_A_3, e_A_5_C, e_A_3_C);
  or or_8 (s_A, s_A_2, s_A_4_C);
  and and_15 (s_A_4_C, set, step_4, instr[15], instr[5]);
  and and_16 (s_D_4_C, set, step_4, instr[15], instr[4]);
  and and_17 (s_RAM_4_C, set, step_4, instr[15], instr[3]);
  buf or_9 (s_RAM_AR, s_RAM_AR_3);  // OR_Gate
  and and_18 (e_A_5_C, enable, step_5, jmp, instr[15]);
  buf or_10 (e_RAM, e_RAM_3_C);  // OR_Gate
  buf or_11 (s_RAM, s_RAM_4_C);  // OR_Gate
  and and_19 (s_IAR_5_C, set, step_5, jmp, instr[15]);
  or or_12 (or_12_out, zr, not_ng);
  and jgt (jgt_out, instr[2], instr[1], instr[0], not_zr, not_ng);
  and jeq (jeq_out, instr[2], instr[1], instr[0], zr);
  and jge (jge_out, instr[2], instr[1], instr[0], or_12_out);
  and jlt (jlt_out, instr[2], instr[1], instr[0], not_zr, ng);
  buf or_13 (e_D, e_D_2_C);  // OR_Gate
  buf or_14 (s_D, s_D_4_C);  // OR_Gate
  and and_20 (e_IAR_6, enable, controlled_buffer_1_out);
  not not_6 (not_6_out, jmp);
  and jne (jne_out, instr[2], instr[1], instr[0], not_zr);
  or or_15 (or_15_out, zr, ng);
  assign controlled_buffer_1_out = not_6_out ? step_6 : 1'bz;  // Controlled_Buffer controlled_buffer_1
  and jle (jle_out, instr[2], instr[1], instr[0], or_15_out);
  and u_jmp (jmp_out, instr[2], instr[1], instr[0]);
  or or_16 (s_TMP, s_TMP_2_C, s_TMP_6);
  and and_21 (s_TMP_6, set, controlled_buffer_1_out);
  or or_17 (or_17_out, jgt_out, jne_out, jeq_out, jle_out, jge_out, jmp_out, jlt_out);
  and and_22 (e_INC_7, enable, f_7);
  and and_23 (jmp, instr[15], or_17_out);
  not not_7 (not_7_out, jmp);
  assign f_7 = not_7_out ? step_7 : 1'bz;  // Controlled_Buffer controlled_buffer_2
  or or_18 (e_ACC, e_ACC_4_C, e_ACC_8);
  or or_19 (s_ACC, s_ACC_3_C, s_ACC_7);
  and and_24 (s_ACC_7, set, f_7);
  and and_25 (e_ACC_8, enable, controlled_buffer_3_out);
  not not_8 (not_8_out, jmp);
  assign controlled_buffer_3_out = not_8_out ? step_8 : 1'bz;  // Controlled_Buffer controlled_buffer_3
  and and_26 (zx, instr[11], not_9_out);
  and and_27 (nx, instr[10], not_9_out);
  and and_28 (zy, instr[9], not_9_out);
  and and_29 (ny, instr[8], not_9_out);
  or or_20 (f, instr[7], f_7);
  and and_30 (no, instr[6], not_9_out);
  and and_31 (s_IAR_8, set, controlled_buffer_3_out);
  not not_9 (not_9_out, step_7);
  buf or_21 (e_INC, e_INC_7);  // OR_Gate

  // Other names for the same wires on the sheet: j3 = instr[0]; not_j3 = instr[0]; j2 = instr[1]; not_j2 = instr[1];
  //   j1 = instr[2]; not_j1 = instr[2]; no_3 = instr[6]; f_3 = instr[7]; ny_3 = instr[8]; zy_3 = instr[9];
  //   nx_3 = instr[10]; zx_3 = instr[11]; i = instr[15]

  // Notes on the sheet:
  //   IAR
  //   ROM_AR
  //   ROM
  //   IR
  //   A
  //   RAM_AR
  //   RAM
  //   D
  //   TMP
  //   ACC
  //   F
  //   INC
endmodule
